# Fritzing sketch Fritz JNE Autopilot V3 (saved by Fritzing 0.8.6b)
breadboards: 1

parts:
  LCD1 = LCD screen
  C1 = Ceramic Capacitor [capacitance=100nF package="100 mil [THT, multilayer]"]
  C2 = Ceramic Capacitor [capacitance=100nF package="100 mil [THT, multilayer]"]
  C3 = Ceramic Capacitor [capacitance=100nF package="100 mil [THT, multilayer]"]
  C4 = Ceramic Capacitor [capacitance=100nF package="100 mil [THT, multilayer]"]
  C5 = Ceramic Capacitor [capacitance=100nF package="100 mil [THT, multilayer]"]
  IC2 = SP3232E [package="DIP16 [THT]"]
  Part3 = IMU Digital Combo Board 6DOF
  S1 = Pushbutton [package="[THT]"]
  S2 = Pushbutton [package="[THT]"]
  S3 = Pushbutton [package="[THT]"]
  S4 = Pushbutton [package="[THT]"]
  S5 = Pushbutton [package="[THT]"]
  S6 = Pushbutton [package="[THT]"]
  S7 = Pushbutton [package="[THT]"]
  S8 = Pushbutton [package="[THT]"]
  S9 = Pushbutton [package="[THT]"]
  S10 = Pushbutton [package="[THT]"]
  S11 = Pushbutton [package="[THT]"]
  S12 = Pushbutton [package="[THT]"]
  S13 = Toggle Switch [package=THT]
  J1 = shrouded pin header, 10 pins [form="♂ (shrouded male)"]
  J2 = shrouded pin header, 10 pins [form="♂ (shrouded male)"]
  S14 = Toggle Switch [package=THT]  # not connected
  S15 = Toggle Switch [package=THT]
  R4 = Rotary Potentiometer (Small) [maximum_resistance=10kΩ package=THT]
  R8 = Rotary Potentiometer (Small) [maximum_resistance=10kΩ package=THT]
  R7 = Rotary Potentiometer (Small) [maximum_resistance=100kΩ package=THT]
  Arduino2 = Arduino Mega 2560 (Rev3)
  Arduino1 = Arduino Mega 2560 (Rev3)
  Part4 = Arduino Mega 2560 (Rev3)
  GLCD_128x1 = 128 x 64 Graphic LCD  # not connected

nets:
  GND: LCD1.VSS, LCD1.V0, LCD1.R/W, LCD1.LED-, C1.0, C3.0, C4.1, IC2.Out_2, Part3.GND, S13.L1, J1.pin3, S15.L1, R4.leg1, R8.leg1, R7.leg1, Arduino2.GND, Arduino1.GND, Part4.GND
  VDD: LCD1.VDD, LCD1.LED+, Part3.3.3V, S15.L2, R7.leg2, Arduino1.5V
  N1: LCD1.RS, Arduino1.D41
  N2: LCD1.E, LCD1.DB0, Arduino1.D43
  N3: LCD1.DB4, Arduino1.D45
  N4: LCD1.DB5, Arduino1.D47
  N5: LCD1.DB6, Arduino1.D49
  N6: LCD1.DB7, Arduino1.D51
  N7: C1.1, IC2.Pin_2_V+
  N8: C2.0, IC2.Pin_3_C1-
  N9: C2.1, IC2.Pin_1_C1+
  N10: C3.1, IC2.Pin_6_V-
  N11: C4.0, IC2.Out_1, S13.L2, R4.leg2, R8.leg2, Arduino2.5V
  N12: C5.0, IC2.Pin_5_C2-
  N13: C5.1, IC2.Pin_4_C2+
  N14: IC2.Pin_9_R2OUT, Arduino2.D16_PWM/TX2
  N15: IC2.Out_5, Arduino2.D17_PWM/RX2
  N16: Part3.SDA, Arduino1.D20/SDA
  N17: Part3.SCL, Part3.INT1, Arduino1.D21/SCL
  N18: S1.Pin_1, S1.Pin_2, S4.Pin_2, S7.Pin_2, S10.Pin_1, S10.Pin_2
  N19: S1.Pin_3, S1.Pin_4, S2.Pin_3, S2.Pin_4, S3.Pin_3, S3.Pin_4, Arduino1.D23
  N20: S2.Pin_1, S2.Pin_2, S5.Pin_2, S8.Pin_2, S11.Pin_1, S11.Pin_2
  N21: S3.Pin_1, S3.Pin_2, S6.Pin_1, S6.Pin_2, S9.Pin_2, S12.Pin_2, J2.pin2, J2.pin3, J2.pin4, J2.pin5
  N22: S4.Pin_3, S4.Pin_4, S5.Pin_3, S5.Pin_4, S6.Pin_3, S6.Pin_4, Arduino1.D25
  N23: S7.Pin_3, S7.Pin_4, S8.Pin_3, S8.Pin_4, S9.Pin_3, S9.Pin_4, Arduino1.D27
  N24: S10.Pin_3, S10.Pin_4, S11.Pin_3, S11.Pin_4, S12.Pin_3, S12.Pin_4, Arduino1.D29
  N25: S13.COM, Arduino1.D48
  N26: J1.pin1, Arduino1.D17_PWM/RX2
  N27: J1.pin5, Arduino1.D16_PWM/TX2
  N28: S15.COM, Arduino1.D46
  N29: R4.wiper, Arduino1.A4
  N30: R8.wiper, R7.wiper, Arduino1.A2
  N31: Arduino2.D14/TX3, Arduino1.D15/RX3
  N32: Arduino1.D19/RX1, Part4.D18/TX1
  N33: Arduino1.D18/TX1, Part4.D19/RX1

notes:
  GPS INPUT
  RS232 in from GPS or PC navigation software.
  Black, Garmin pin5, ground.
  Red, Garmin Rx, Pin 2.
  Green, Garmin Tx Pin 3.
  LCD could be rewired. There are two wires to +5V and 4 wires to Grnd. Could do at LCD so extra wires don't need to go to Arduino.
  NOTE 2 x 16 LCD shown mine is 4 x 20.
  Some colors are white with stripe of shown color.
  Pololu MinIMU-9
  9 DOF gyro Compass
  External wiring with telephone RJ-11 6P4C jacks and wire
  KEYPAD
  (no componenet available)
  1 2 3
  4 5 6
  7 8 9
  * 0 #
  Column Wiring
  1 - BLK, pin 31
  2 - BLK/W, pin 33
  3 - BLU, pin 35
  Row Wiring
  3 - OR, pin 23
  6 - OR/W, pin25
  9 - GR/W, pin 27
  # - GR, pin 29
  OUTPUT TO RUDDER CONTROL
  (Telephone Connector - no symbol)
  Output on Serial2
  Orange to TREX pin SI
  Blue to TREX pin SO
  Green to TREX grnd
  STEERING ENABLE SWITCH sw1 (pin 48)
  Must be on to select steering modes and steer. If sw1 already on pressing key 1 sets compass mode and captures current heading as heading_to_steer. If turned off HTS set to 0.
  RUDDER POSITION FEEDBACK
  Mounted on rudder shaft.
  (Analog Pin 4)
  Honeywell Hall Effect rotary Position Sensor 785-RTY090LVNAX
  .5 V to 4.5 V = -/+45 deg, www.mouser.com
  REMOTE KEYPAD (optional)
  Hard wired in parallel using eithernet cable and plug. Uses eithernet cble and connectors
  NOTES
  JNE Autopilot V1 10/25/13
  V1 uses the Wagener onboard motor controller. see the desription below for Output to Rudder Control
  V2 is wired to use the Pololu TREX motor controller with serial input.
  10 k pot(not required) use for Knob steering, gain adjustments, etc.
  REMOTE SWITCH AND POTENTIOMETER (Optional)
  SW2 on to enable steering.
  SW2, Function to disable automated steering (open clutch/solenoid) so steering can be done manually. Important safety feature if remote controller is used. SW@ to Pin 46
  10k Pot used for Knob Steering, Keypad 8 to engage. Knob to A2. Use local or remote Knob, not both.
  Use switch and potentiometer with either hard wired or serial remote.
  SERIAL REMOTE
  uses separate Arduino MEGA
  Run Software:
  Serial_Remote_Version
  ADAFRUIT
  2.8" TFT Touch Shield for Arduino v2 -
  ID: 1651 Manufactured by: Adafruit
  KEYPAD
  WIRED AS OTHER KEYPADS
  To Vin power Supply
  via Serial 6 wire cable
  Serial Remote
  Wire
  TX1 to RX1
  RX1 to TX1

custom parts:
  SP3232E: SPIEX ADAPTER, RS232 TO TTL
