# Fritzing sketch Fritz JNE RF Remote (saved by Fritzing 0.9.0b)
perfboards: 1

parts:
  Part1 = Arduino Micro (Rev3)
  JP8 = Header 8 [package=1x08_smd]  # not connected
  Keypad4x1 = Keypad Membran 4x4
  JP7 = Header 5x2 [package=2x5-ra]
  Part2 = NRF24L01+ Breakout Board
  JP5 = Header 10 [package=1x10-2mm-smd]
  4x20_LCD_screen_w/Green_Screen1 = 4x20 LCD screen w/Green Screen
  R2 = Resistor [tolerance=±5% resistance=330 package=THT]
  U1 = LIPO-110mAh [package=lipo-110]
  S1 = Toggle Switch [package=THT]

nets:
  N1: Part1.MOSI, JP7.5, Part2.MOSI
  N2: Part1.D2/SDA, JP7.8, Part2.CE
  N3: Part1.D3/SCL, JP7.7, Part2.CS
  N4: Part1.D6_PWM/A7, Keypad4x1.Pin1
  N5: Part1.D7, Keypad4x1.Pin2
  N6: Part1.D8_PWM/A8, Keypad4x1.Pin3
  N7: Part1.D9_PWM/A9, Keypad4x1.Pin4
  N8: Part1.D10_PWM/A10, Keypad4x1.Pin5
  N9: Part1.D11_PWM, Keypad4x1.Pin6
  N10: Part1.D12_PWM/A11, Keypad4x1.Pin7
  N11: Part1.SCK, JP7.6, Part2.SCK
  N12: Part1.MISO, JP7.4, Part2.MISO
  GND: Part1.GND, JP7.10, Part2.GND, 4x20_LCD_screen_w/Green_Screen1.VSS, 4x20_LCD_screen_w/Green_Screen1.R/W, R2.Pin_1
  5V: Part1.5V, JP7.9, Part2.VCC, JP5.3, 4x20_LCD_screen_w/Green_Screen1.VDD, 4x20_LCD_screen_w/Green_Screen1.LED+
  N13: Part1.A5, JP5.5, 4x20_LCD_screen_w/Green_Screen1.RS
  N14: Part1.A4, JP5.6, 4x20_LCD_screen_w/Green_Screen1.E
  N15: Part1.A3, JP5.7, 4x20_LCD_screen_w/Green_Screen1.DB4
  N16: Part1.A2, JP5.8, 4x20_LCD_screen_w/Green_Screen1.DB5
  N17: Part1.A0, JP5.10, 4x20_LCD_screen_w/Green_Screen1.DB7
  N18: Part1.D13_PWM, 4x20_LCD_screen_w/Green_Screen1.V0
  N19: JP5.9, 4x20_LCD_screen_w/Green_Screen1.DB6
  N20: 4x20_LCD_screen_w/Green_Screen1.LED-, R2.Pin_0
  N21: U1.+, S1.COM
  N22: U1.-, S1.L2

notes:
  KEYPAD
  4 x 4 shown but use a 3 x 4 with 7 wires
  rowPins[ROWS] = {7,12,11,9};
  colPins[COLS] = {8,6,10};
  RF24 power Supply
  Yourduino.com RA-109901
  5V in 3.3 V to RF24
  IMPORTANT use 3.3 v if going directly to RF module
  LCD Pin to Arduino Micro Pin
  1 Vss to Grnd
  2 Vdd to 5v
  3 Vo, Contrast, PWM 13
  4 RS to A5
  5 R/W to Grnd
  6 E to A4
  7 - 10 no connection
  11 DB4 to A3
  12 DB5 to A2
  13 DB6 to A1
  14 DB7 to A0
  15LED+ to 5v
  16 LED- to 390 ohm resistor to Grnd
  LCD(RS, E, D4, D5, D6, D7)
  LCD(A5, A4, A3, A2, A1, A0)
  CAUTION!
  Radio must have 3.3 V in not 5 V
  Wiring for the RF24L01+
  Note the RF24 uses the SPI bus, so does the TFT. They share all of the same pins except the CE pin
  1 Ground to ground
  2 VCC must be 3.3 V
  3 CE to Micro D2, Mega 9 or other
  I use 9 on the Autopilot
  but I use 11 on Remote with TFT
  because TFT uses 9
  4 CSN to Micro D3, Mega 10
  5 SCK to Micro SCK, Mega 52
  6 MOSI to Micro MOSI, Mega 51
  7 MISO to Micro MISO, Mega 50
  8 IRQ not used
  CE and CSN are configurable in the code as:
  RF24 radio(CE,CSN);
  Battery
  ANKER 6000 mAh
  Use fabricated Micro USB cable

custom parts:
  Keypad Membran 4x4: Membrane Keypad 4x4 Matrix
  4x20 LCD screen w/Green Screen: A standard character display with 4x20 characters.
